# Fritzing sketch NADES Sketch (saved by Fritzing 0.4.2b)
breadboards: 1

parts:
  Arduino1 = Arduino
  R1 = Resistor [resistance=220 package=THT]
  R1_2 = Resistor [resistance=220 package=THT]
  R1_3 = Resistor [resistance=220 package=THT]
  R2 = Resistor [resistance=10k package=THT]
  R2_2 = Resistor [resistance=10k package=THT]
  R2_3 = Resistor [resistance=10k package=THT]
  U1 = mystery part, 4 pins [chip_label=QRB1134 spacing=300mil]

nets:
  N1: Arduino1.aref, R1.Pin_0, U1.pin1
  N2: Arduino1.GND, U1.pin2, U1.pin3
  N3: Arduino1.D7, R2_3.Pin_0, U1.pin4
  N4: Arduino1.D6, R2_2.Pin_0
  N5: Arduino1.D5, R2.Pin_0
  N6: Arduino1.+5V, R1.Pin_1, R1_2.Pin_1, R1_3.Pin_1, R2.Pin_1, R2_2.Pin_1, R2_3.Pin_1
